// Digital circuit boot-rom.dig as structural Verilog
module boot_rom (
  input  [23:0] Addr,
  input  En,
  output [31:0] Out_code
);

  wire [23:0] barrelshifter_1_out;

  BarrelShifter #(.Bits(24), .direction("right")) barrelshifter_1 (
    .in(Addr), .shift(5'b00010), .out(barrelshifter_1_out));
  ROM #(.AddrBits(24), .Bits(8)) rom_1 (.A(barrelshifter_1_out), .sel(En), .D(Out_code[7:0]));
  ROM #(.AddrBits(24), .Bits(8)) rom_2 (.A(barrelshifter_1_out), .sel(En), .D(Out_code[15:8]));
  ROM #(.AddrBits(24), .Bits(8)) rom_3 (.A(barrelshifter_1_out), .sel(En), .D(Out_code[23:16]));
  ROM #(.AddrBits(24), .Bits(8)) rom_4 (.A(barrelshifter_1_out), .sel(En), .D(Out_code[31:24]));

  // Notes on the sheet:
  //   contents of rom_1 (hex, n*v repeats v):
  //   7f,f3,37,b7,37,83,23,13,93,e3,37,13,11*f3,37,13,f3,93,13,93,13
  //   ,93,93,97,e7
  //   contents of rom_2 (hex, n*v repeats v):
  //   0,12,3,3,3e,45,80,3,83,e8,3,3,11*13,2e,e,13,2,3,3,e,e,5,0,80
  //   contents of rom_3 (hex, n*v repeats v):
  //   5*0,3,b3,13,13,c3,0,3,13,10,20,30,40,50,10,20,30,40,40,0,8e,e
  //   contents of rom_4 (hex, n*v repeats v):
  //   80,30,40,2,2,4*0,ff,c0,10,30,4*f1,30,4*34,30,0,80,30,6*0,82,f8
endmodule
