// Digital circuit i2c-slave.dig as structural Verilog
module i2c_slave (
  input  SCL,
  input  SDA,
  input  [6:0] Address,
  input  [7:0] Data_in,
  output SDA_out,
  output Out_en,
  output [7:0] Data_out,
  output [7:0] Addr_out
);

  wire Addr_invalid, and_1_out, and_4_out, and_5_out, and_7_out, and_8_out, ask_in, comparator_1_eq,
       control_sig, data_bit, dstatus_en, or_2_out, or_3_out, s1_end, s2_end, s2_readend, slave_s0, slave_s1,
       slave_s2, slave_s3, start_sig, stop_sig, xor_1_out;
  wire [1:0] dstatus, I2C_status;
  wire [7:0] byte_out, Data_out_t, data_send, i2c_master_readdata_1_data_out, i2c_master_readdata_2_data_out,
       i2c_master_readdata_3_data_out;

  and and_1 (and_1_out, control_sig, SDA);
  xor xor_1 (xor_1_out, SDA, data_bit);
  and and_2 (start_sig, control_sig, ~SDA);  // And
  and and_3 (control_sig, xor_1_out, SCL);
  D_FF d_ff_1 (.D(SDA), .C(SCL), .Q(data_bit));  // open: nQ
  or or_1 (stop_sig, and_1_out, Addr_invalid);
  or or_2 (or_2_out, slave_s1, slave_s0);
  and and_4 (and_4_out, stop_sig, ~slave_s0);  // And
  or or_3 (or_3_out, s2_readend, and_4_out);
  and and_5 (and_5_out, start_sig, ~or_2_out, ~stop_sig);  // And
  _4_status_mechine _4_status_mechine_1 (
    .Clock(SCL), .nexten_0(start_sig), .nexten_1(s1_end), .nexten_2(s2_end), .nexten_3(Out_en),
    .direct_statusen(dstatus_en), .direct_status(dstatus), .falling_edge_status(4'b0111),
    .Status_cur(I2C_status));
  i2c_master_readdata i2c_master_readdata_1 (
    .en(start_sig), .Clock(SCL), .SDA_in(SDA), .SDA(SDA_out), .status(s1_end),
    .Data_out(i2c_master_readdata_1_data_out));
  Comparator #(.Bits(7)) comparator_1 (.a(byte_out[7:1]), .b(Address), .eq(comparator_1_eq));  // open: gt, lt
  assign dstatus = or_3_out ? 2'b00 : 2'bz;  // Driver driver_1
  assign dstatus = and_5_out ? 2'b01 : 2'bz;  // Driver driver_2
  PullDown pulldown_1 (.out(byte_out[0]));
  and and_6 (Addr_invalid, ~comparator_1_eq, slave_s1, s1_end);  // And
  assign byte_out = s1_end ? i2c_master_readdata_1_data_out : 8'bz;  // Driver driver_3
  assign dstatus_en = or_3_out ? 1'b1 : 1'bz;  // Driver driver_4
  assign dstatus_en = and_5_out ? 1'b1 : 1'bz;  // Driver driver_5
  Decoder #(.Selector_Bits(2)) decoder_1 (
    .sel(I2C_status), .out_0(slave_s0), .out_1(slave_s1), .out_2(slave_s2), .out_3(slave_s3));
  and and_7 (and_7_out, ~byte_out[0], s1_end);  // And
  i2c_master_readdata i2c_master_readdata_2 (
    .en(and_7_out), .Clock(SCL), .SDA_in(SDA), .SDA(SDA_out), .status(s2_end),
    .Data_out(i2c_master_readdata_2_data_out));
  Register #(.Bits(8)) register_1 (.D(byte_out), .C(SCL), .en(s2_end), .Q(Addr_out));
  i2c_master_readdata i2c_master_readdata_3 (
    .en(s2_end), .Clock(SCL), .SDA_in(SDA), .SDA(SDA_out), .status(Out_en),
    .Data_out(i2c_master_readdata_3_data_out));
  Register #(.Bits(8)) register_2 (.D(byte_out), .C(SCL), .en(Out_en), .Q(Data_out_t));
  assign byte_out = s2_end ? i2c_master_readdata_2_data_out : 8'bz;  // Driver driver_6
  and and_8 (and_8_out, s1_end, byte_out[0]);
  assign byte_out = Out_en ? i2c_master_readdata_3_data_out : 8'bz;  // Driver driver_7
  assign Data_out = ~byte_out[0] ? Data_out_t : 8'bz;  // DriverInvSel driverinvsel_1
  Register #(.Bits(8)) register_3 (.D(Data_in), .C(SCL), .en(slave_s0), .Q(data_send));
  i2c_master_senddata i2c_master_senddata_1 (
    .Data_in(data_send), .en(and_8_out), .Clock(SCL), .SDA_in(SDA), .SDA(SDA_out), .status(s2_readend),
    .ack(ask_in));

  // Other names for the same wires on the sheet: Addr_self[6:0] = Address; rw = byte_out[0];
  //   dev_addr[6:0] = byte_out[7:1]; s3_end = Out_en; scl_in = SCL; sda_in = SDA

  // Notes on the sheet:
  //   s0: wait start
  //   s1: read dev address
  //   s2: read write mem address or send data
  //   s3: read write data
endmodule
