// Digital circuit int-except-unit.dig as structural Verilog
module int_except_unit (
  input  [31:0] Exception_code,
  input  Interrupt_timer,
  input  Interrupt_peripheral,
  input  [31:0] csr1_in,
  input  [31:0] csr2_in,
  input  Clock,
  input  [31:0] PC_Addr,
  input  [31:0] PC_ip,
  output [11:0] csr_readaddr1,
  output [11:0] csr_readaddr2,
  output PC_EN,
  output [11:0] csr_waddr,
  output csr_we,
  output [31:0] csr_out,
  output En_jmp,
  output [31:0] Addr_jmp
);

  wire and_5_out, and_6_out, EN_excep, EN_ie, EN_int, step1, step2, step3, step4, step5, step6, step7, step8;
  wire [0:0] exception_iop;
  wire [2:0] ie_counter;
  wire [30:0] excep_code;
  wire [31:0] mie_in, mip_in, mstatus_in;

  or or_1 (EN_int, Interrupt_timer, Interrupt_peripheral);
  PullUp #(.Bits(32)) pullup_1 (.out(Exception_code));
  not not_1 (EN_excep, exception_iop[0]);
  and and_1 (csr_we, EN_excep, step1);
  and and_2 (csr_we, EN_excep, step2);
  and and_3 (csr_we, EN_excep, step3);
  and and_4 (csr_we, EN_excep, step4);
  assign csr_waddr[0] = csr_we ? 1'b0 : 1'bz;  // Driver driver_1
  assign csr_waddr[0] = csr_we ? 1'b1 : 1'bz;  // Driver driver_2
  assign csr_waddr[0] = csr_we ? 1'b1 : 1'bz;  // Driver driver_3
  assign csr_waddr[0] = csr_we ? 1'b0 : 1'bz;  // Driver driver_4
  assign csr_out = csr_we ? {mstatus_in[31:8], EN_ie, mstatus_in[6:4], 1'b0, mstatus_in[2:0]} : 32'bz;  // Driver driver_5
  assign csr_out = csr_we ? PC_Addr : 32'bz;  // Driver driver_6
  assign csr_out = csr_we ? PC_ip : 32'bz;  // Driver driver_7
  assign csr_out = csr_we ? {1'b0, excep_code} : 32'bz;  // Driver driver_8
  assign csr_readaddr2 = csr_we ? 12'h305 : 12'bz;  // Driver driver_9
  assign csr_readaddr2 = step1 ? 12'h300 : 12'bz;  // Driver driver_10
  assign Addr_jmp = csr_we ? csr2_in : 32'bz;  // Driver driver_11
  and and_5 (and_5_out, step2, EN_int);
  assign csr_readaddr2 = step3 ? 12'h304 : 12'bz;  // Driver driver_12
  Counter #(.Bits(3)) counter_1 (.en(1'b1), .C(Clock), .clr(PC_EN), .out(ie_counter));  // open: ovf
  assign csr_readaddr1 = step3 ? 12'h344 : 12'bz;  // Driver driver_13
  Decoder #(.Selector_Bits(3)) decoder_1 (
    .sel(ie_counter), .out_0(step1), .out_1(step2), .out_2(step3), .out_3(step4), .out_4(step5),
    .out_5(step6), .out_6(step7), .out_7(step8));
  Register #(.Bits(32)) register_1 (.D(csr2_in), .C(Clock), .en(step1), .Q({mstatus_in[31:4], EN_ie, mstatus_in[2:0]}));
  assign mie_in = step3 ? csr2_in : 32'bz;  // Driver driver_14
  assign mip_in = step3 ? csr1_in : 32'bz;  // Driver driver_15
  and and_6 (and_6_out, EN_int, EN_ie);
  nor nor_1 (PC_EN, and_6_out, EN_excep);
  PullDown pulldown_1 (.out(csr_we));
  PullDown #(.Bits(32)) pulldown_2 (.out(Addr_jmp));
  // Pins of 1 and 12 bits meet at csr_waddr
  // Pins of 1 and 12 bits meet at 12'h341
  // Pins of 1 and 12 bits meet at 12'h343
  // Pins of 1 and 12 bits meet at 12'h300
  // Pins of 1 and 12 bits meet at 12'h342

  assign En_jmp = csr_we;

  // Other names for the same wires on the sheet: C = Clock; csr_rdaddr1[11:0] = csr_readaddr1;
  //   csr_rdaddr2[11:0] = csr_readaddr2; exception_iop[31:1] = excep_code; mstatus_in[3] = EN_ie

  // Notes on the sheet:
  //   mstatus
  //   mepc
  //   mtval
  //   mcause
endmodule
